# Fritzing sketch MotorDriverSketch (saved by Fritzing 0.8.7b)

parts:
  Part1 = Arduino Uno (Rev3)
  S1 = H-Bridge with L298N
  BAT1 = 18650 battery holder [package=battery-18650-kit]
  BAT2 = 18650 battery holder [package=battery-18650-kit]
  BAT3 = 18650 battery holder [package=battery-18650-kit]
  M1 = DC Motor
  M2 = DC Motor

nets:
  N1: Part1.D10_PWM/SS, S1.ENB
  N2: Part1.D11_PWM/MOSI, S1.ENA
  N3: Part1.D3_PWM, S1.IN4
  N4: Part1.D4, S1.IN3
  N5: Part1.D6_PWM, S1.IN2
  N6: Part1.D7, S1.IN1
  GND: Part1.GND, S1.GND, BAT1.-
  VIN: Part1.VIN, S1.12V, BAT3.+
  N7: S1.M1-01, M2.pin_2
  N8: S1.M1-02, M2.pin_1
  N9: S1.M2-01, M1.pin_2
  N10: S1.M2-02, M1.pin_1
  N11: BAT1.+, BAT2.-
  N12: BAT2.+, BAT3.-

custom parts:
  H-Bridge with L298N: h-bridge
  18650 battery holder: 18650 Battery Holder
